// Logisim project Portas.circ as structural Verilog: 1 circuit, main circuit main
module main (
  input  in_1,
  input  in_2,
  input  in_3,
  input  in_4,
  input  in_5,
  input  in_6,
  input  in_7,
  input  in_8,
  input  in_9,
  input  in_10,
  output out_11,
  output out_12,
  output out_13,
  output out_14,
  output out_15,
  output out_16,
  output out_17,
  output out_18,
  output out_19,
  output Cout
);

  wire and_2_out, and_3_out, and_4_out, and_5_out, and_6_out, and_7_out, and_8_out, not_1_out, or_3_out,
       or_4_out, or_5_out, xor_3_out, xor_4_out;

  not not_1 (not_1_out, in_9);
  not not_2 (out_11, in_1);
  and and_1 (out_12, in_1, in_2);
  or or_1 (out_14, in_1, in_2);
  xor xor_1 (out_15, in_1, in_2);
  xnor xnor_1 (out_16, in_1, in_2);
  or or_2 (out_18, not_1_out, in_10);
  xor xor_2 (out_13, in_5, in_8);
  and and_2 (and_2_out, in_5, in_8);
  xor xor_3 (xor_3_out, in_4, in_7);
  and and_3 (and_3_out, in_4, in_7);
  and and_4 (and_4_out, in_4, and_2_out);
  and and_5 (and_5_out, in_7, and_2_out);
  xor xor_4 (xor_4_out, in_3, in_6);
  and and_6 (and_6_out, in_3, in_6);
  and and_7 (and_7_out, in_3, or_4_out);
  and and_8 (and_8_out, in_6, or_4_out);
  xor xor_5 (out_17, xor_3_out, and_2_out);
  or or_3 (or_3_out, and_3_out, and_4_out);
  or or_4 (or_4_out, or_3_out, and_5_out);
  xor xor_6 (out_19, xor_4_out, or_4_out);
  or or_5 (or_5_out, and_6_out, and_7_out);
  or or_6 (Cout, or_5_out, and_8_out);

  // Notes on the sheet:
  //   Numero B (Binário)
  //   Numero A (Binário)
  //   Cin
  //   Cin
  //   Cout
  //   Cout
endmodule
